// Logisim project NEW_PC_16_BIT.circ as structural Verilog: 9 circuits, main circuit home
module home (
  input  in_1,
  output [3:0] out_2,
  output [35:0] out_3,
  output [15:0] out_4,
  output [15:0] out_5,
  output [15:0] out_6
);

  wire alu_1_cflag_0, and_1_out, and_2_out, button_2_out, CLK, n7_segment_display_1_p2,
       n7_segment_display_1_p3, not_1_out, or_1_out, or_2_out, or_3_out, or_4_out, or_5_out, RS, Run;
  wire [3:0] counter_1_q;
  wire [7:0] ACC_q, ADDRL_q, ADDRM_q, alu_1_out_0, BR_q, BYTER_q, CODE, CR_q, ram_1_dout, rom_1_data, TMP_q;
  wire [15:0] ADDR, counter_2_q, PC_q;

  TTY #(.cols(64), .rows(16)) tty_1 ();  // open: data, clk, we, clr
  Button button_1 (.out(RS));
  Button button_2 (.out(button_2_out));
  not not_1 (not_1_out, out_3[35]);
  buf or_1 (or_1_out, button_2_out);  // OR_Gate
  assign CLK = not_1_out ? or_1_out : 1'bz;  // Controlled_Buffer controlled_buffer_1
  not not_2 (Run, in_1);
  ROM #(.addrWidth(16)) rom_1 (.addr(ADDR), .data(rom_1_data));
  Counter #(.max('hf), .trigger("falling"), .width(4)) counter_1 (
    .count(1'b1), .Q(counter_1_q), .clk(CLK), .clr(or_2_out));  // open: load, D, carry, up
  or or_2 (or_2_out, RS, out_3[10]);
  Keyboard keyboard_1 ();  // open: clk, re, clr, avail, data
  assign out_4 = out_3[17] ? PC_q : 16'bz;  // Controlled_Buffer controlled_buffer_2
  Counter #(.max('hffff), .width(16)) PC (
    .load(out_3[16]), .D(out_4), .count(out_3[18]), .Q(PC_q), .clk(CLK), .clr(RS));  // open: carry, up
  assign out_4[7:0] = out_3[3] ? rom_1_data : 8'bz;  // Controlled_Buffer controlled_buffer_3
  assign out_4[7:0] = and_1_out ? rom_1_data : 8'bz;  // Controlled_Buffer controlled_buffer_4
  and and_1 (and_1_out, out_3[23], ~Run);  // AND_Gate
  RAM #(.addrWidth(16), .asyncread("true")) ram_1 (
    .addr(ADDR), .we(out_3[24]), .oe(out_3[23]), .clk(CLK), .din(out_4[7:0]), .dout(ram_1_dout));
  Controller controller_1 (.FLGs({1'b0, out_2[2:0]}), .OPcode(CODE), .Steps(counter_1_q), .x(out_3));
  Counter #(.max('hffff), .width(16)) counter_2 (
    .load(out_3[7]), .D(out_4), .count(out_3[5]), .Q(counter_2_q), .carry(out_2[2]), .up(out_3[6]),
    .clk(CLK), .clr(RS));
  assign out_4 = out_3[4] ? counter_2_q : 16'bz;  // Controlled_Buffer controlled_buffer_5
  // RGB_Video #(.height(256), .width(256)) rgb_video_1: pin names not known
  // Output_Display output_display_1: pin names not known; wires that end beside it: out_4[7:0], out_2[1], CLK, out_3[19]
  // _7_Segment_Display 7_segment_display_1: pin names not known; wires that end beside it: RS, n7_segment_display_1_p2, n7_segment_display_1_p3, n7_segment_display_1_p2, n7_segment_display_1_p3
  // EEPROM_Display eeprom_display_1: pin names not known
  assign out_4[7:0] = and_2_out ? ram_1_dout : 8'bz;  // Controlled_Buffer controlled_buffer_6
  and and_2 (and_2_out, out_3[23], Run);
  _7_Segment_Display u_7_segment_display_2 ();  // open: g, f, a, b, e, d, c, dp
  _7_Segment_Display u_7_segment_display_3 ();  // open: g, f, a, b, e, d, c, dp
  Register ADDRM (.D(out_4[7:0]), .en(out_3[13]), .clk(CLK), .Q(ADDRM_q), .clr(RS));
  Register ADDRL (.D(out_4[7:0]), .en(out_3[12]), .clk(CLK), .Q(ADDRL_q), .clr(RS));
  Register BYTER (.D(out_4[7:0]), .en(out_3[9]), .clk(CLK), .Q(BYTER_q), .clr(RS));
  Register IR (.D(out_4[7:0]), .en(out_3[21]), .clk(CLK), .Q(CODE), .clr(RS));
  Register #(.width(16)) MAR (.D(out_4), .en(out_3[22]), .clk(CLK), .Q(ADDR), .clr(RS));
  _7_Segment_Display u_7_segment_display_4 ();  // open: g, f, a, b, e, d, c, dp
  assign out_4[15:8] = out_3[11] ? ADDRM_q : 8'bz;  // Controlled_Buffer controlled_buffer_7
  assign out_4[7:0] = out_3[11] ? ADDRL_q : 8'bz;  // Controlled_Buffer controlled_buffer_8
  assign out_4[7:0] = out_3[8] ? BYTER_q : 8'bz;  // Controlled_Buffer controlled_buffer_9
  Register ACC (.D(out_4[7:0]), .en(out_3[34]), .clk(CLK), .Q(ACC_q), .clr(RS));
  assign out_4[7:0] = out_3[33] ? ACC_q : 8'bz;  // Controlled_Buffer controlled_buffer_10
  assign out_4[7:0] = out_3[31] ? alu_1_out_0 : 8'bz;  // Controlled_Buffer controlled_buffer_11
  assign out_4[7:0] = out_3[29] ? TMP_q : 8'bz;  // Controlled_Buffer controlled_buffer_12
  Register TMP (.D(out_4[7:0]), .en(out_3[30]), .clk(CLK), .Q(TMP_q), .clr(or_3_out));
  assign out_4[7:0] = out_3[27] ? BR_q : 8'bz;  // Controlled_Buffer controlled_buffer_13
  Register BR (.D(out_4[7:0]), .en(out_3[28]), .clk(CLK), .Q(BR_q), .clr(RS));
  assign out_4[7:0] = out_3[25] ? CR_q : 8'bz;  // Controlled_Buffer controlled_buffer_14
  Register CR (.D(out_4[7:0]), .en(out_3[26]), .clk(CLK), .Q(CR_q), .clr(RS));
  ALU alu_1 (
    .Ain_0(ACC_q), .Bin_0(TMP_q), .SS(out_3[32]), .Cflag_0(alu_1_cflag_0), .Nflag_0(out_2[1]),
    .Out_0(alu_1_out_0));
  or or_3 (or_3_out, out_3[2], RS);
  or or_4 (or_4_out, alu_1_cflag_0, or_5_out);
  or or_5 (or_5_out, out_3[20], RS);
  S_R_Flip_Flop s_r_ff_1 (.S(alu_1_cflag_0), .clk(or_4_out), .R(or_5_out), .Q(out_2[0]));  // open: Qn, preset, reset

  assign out_2[3] = 1'b0;
  assign out_5 = out_4;
  assign out_6 = out_4;

  // Other names for the same wires on the sheet: CF = out_2[0]; FLGs[2:0] = out_2[2:0]; NF = out_2[1]; ZF = out_2[2];
  //   Install = in_1; RT = out_3[2]; XO = out_3[3]; CDO = out_3[4]; CDE = out_3[5]; INC = out_3[6]; DCI = out_3[7];
  //   BYO = out_3[8]; BYI = out_3[9]; STR = out_3[10]; AD1O = out_3[11]; AD2O = out_3[11]; ADRO = out_3[11];
  //   AD2 = out_3[12]; AD1 = out_3[13]; JZ = out_3[14]; JC = out_3[15]; J = out_3[16]; PCO = out_3[17];
  //   PCE = out_3[18]; OI = out_3[19]; RF = out_3[20]; II = out_3[21]; MI = out_3[22]; RO = out_3[23]; RI = out_3[24];
  //   CO = out_3[25]; CI = out_3[26]; BO = out_3[27]; BI = out_3[28]; T0 = out_3[29]; TI = out_3[30]; SO = out_3[31];
  //   SS = out_3[32]; AO = out_3[33]; AI = out_3[34]; HLT = out_3[35]; BS[15:0] = out_4; LB[7:0] = out_4[7:0];
  //   MB[7:0] = out_4[15:8]

  // Notes on the sheet:
  //   contents of rom_1 (hex, n*v repeats v):
  //   7 ff e9 b 1 c 0 2f b 0 c 0 2e 8 0 2b 9 0 2e a 0 2e 1 0 2f c 0 30 a 0 2f c 0 2e a 0 30 c 0 2f 7 0 d 7
  //   0 3 65467*0 3 0 30 2 ff f4 4 5 7 ff ec b 0 c 0 2 c 0 1 c 0 0 6
endmodule

module teste (
  input  in_1,
  input  in_2,
  input  in_3,
  input  in_4,
  input  in_5,
  input  [23:0] in_6,
  input  [23:0] in_7,
  input  in_8,
  input  [23:0] in_9,
  input  [23:0] in_10,
  input  [23:0] in_11,
  input  [23:0] in_12
);

  wire button_1_out, button_2_out, button_3_out, clock_1_out, clock_2_out, clock_3_out, counter_1_q,
       counter_2_carry, counter_3_carry, counter_4_carry, counter_5_carry, counter_6_q, counter_7_q,
       counter_8_carry, counter_9_carry;
  wire [5:0] rgb_video_1_p4, rgb_video_1_p5;
  wire [6:0] counter_4_q, counter_5_q;
  wire [7:0] rgb_video_3_p4, rgb_video_3_p5;
  wire [23:0] rgb_video_1_p6, rgb_video_2_p6, rgb_video_3_p6;

  Clock clock_1 (.out(clock_1_out));
  Button button_1 (.out(button_1_out));
  Counter #(.max('h1), .width(1)) counter_1 (
    .Q(counter_1_q), .clk(counter_3_carry));  // open: load, D, count, carry, up, clr
  // RGB_Video #(.height(64), .width(64)) rgb_video_1: pin names not known; wires that end beside it: in_1, clock_1_out, in_2, rgb_video_1_p4, rgb_video_1_p5, rgb_video_1_p6
  Counter #(.max('h3f), .width(6)) counter_2 (
    .Q(rgb_video_1_p4), .carry(counter_2_carry), .clk(clock_1_out), .clr(button_1_out));  // open: load, D, count, up
  Counter #(.max('h3f), .width(6)) counter_3 (
    .Q(rgb_video_1_p5), .carry(counter_3_carry), .clk(counter_2_carry), .clr(button_1_out));  // open: load, D, count, up
  Selector_24_bits selector_24_bits_1 (.in_2(in_6), .in_3(in_7), .in_1(counter_1_q), .out_4(rgb_video_1_p6));
  Button button_2 (.out(button_2_out));
  Clock clock_2 (.out(clock_2_out));
  Counter #(.max('h7f), .width(7)) counter_4 (
    .Q(counter_4_q), .carry(counter_4_carry), .clk(clock_2_out), .clr(button_2_out));  // open: load, D, count, up
  Counter #(.max('h7f), .width(7)) counter_5 (
    .Q(counter_5_q), .carry(counter_5_carry), .clk(counter_4_carry), .clr(button_2_out));  // open: load, D, count, up
  Counter #(.max('h1), .width(1)) counter_6 (
    .Q(counter_6_q), .clk(counter_5_carry));  // open: load, D, count, carry, up, clr
  // RGB_Video rgb_video_2: pin names not known; wires that end beside it: in_3, clock_2_out, in_4, counter_4_q, counter_5_q, rgb_video_2_p6
  Selector_24_bits selector_24_bits_2 (.in_2(in_9), .in_3(in_10), .in_1(counter_6_q), .out_4(rgb_video_2_p6));
  Clock clock_3 (.out(clock_3_out));
  Button button_3 (.out(button_3_out));
  Counter #(.max('h1), .width(1)) counter_7 (
    .Q(counter_7_q), .clk(counter_9_carry));  // open: load, D, count, carry, up, clr
  // RGB_Video #(.height(256), .width(256)) rgb_video_3: pin names not known; wires that end beside it: in_5, clock_3_out, in_8, rgb_video_3_p4, rgb_video_3_p5, rgb_video_3_p6
  Counter counter_8 (
    .Q(rgb_video_3_p4), .carry(counter_8_carry), .clk(clock_3_out), .clr(button_3_out));  // open: load, D, count, up
  Counter counter_9 (
    .Q(rgb_video_3_p5), .carry(counter_9_carry), .clk(counter_8_carry), .clr(button_3_out));  // open: load, D, count, up
  Selector_24_bits selector_24_bits_3 (.in_2(in_11), .in_3(in_12), .in_1(counter_7_q), .out_4(rgb_video_3_p6));

  // Notes on the sheet:
  //   64x64p
  //   128x128p
  //   256x256p
endmodule

module ALU (
  input  [7:0] Ain_0,
  input  SS,
  input  [7:0] Bin_0,
  output [7:0] Out_0,
  output Cflag_0,
  output Nflag_0
);

  wire not_1_out, subtractor_1_bout;
  wire [7:0] adder_1_out, subtractor_1_out;

  Adder adder_1 (.a(Ain_0), .b(Bin_0), .out(adder_1_out), .cin(1'b0), .cout(Cflag_0));
  Subtractor subtractor_1 (.a(Ain_0), .b(Bin_0), .out(subtractor_1_out), .bin(1'b0), .bout(subtractor_1_bout));
  assign Out_0 = not_1_out ? adder_1_out : 8'bz;  // Controlled_Buffer controlled_buffer_1
  not not_1 (not_1_out, SS);
  assign Out_0 = SS ? subtractor_1_out : 8'bz;  // Controlled_Buffer controlled_buffer_2
  and and_1 (Nflag_0, subtractor_1_bout, SS);
endmodule

module Controller (
  input  [3:0] FLGs,
  input  [7:0] OPcode,
  input  [3:0] Steps,
  output [35:0] x
);

  wire and_2_out, and_3_out, and_4_out, and_8_out, and_9_out, and_10_out, and_11_out, and_12_out, and_13_out,
       and_14_out, and_15_out, and_16_out, and_17_out, and_18_out, and_19_out, and_20_out, and_21_out,
       and_22_out, and_23_out, and_24_out, and_25_out, and_26_out, and_27_out, and_28_out, and_29_out,
       and_30_out, and_31_out, and_32_out, and_33_out, and_34_out, and_35_out, and_36_out, and_37_out,
       and_38_out, and_39_out, and_40_out, and_41_out, and_43_out, and_44_out, and_45_out, and_46_out,
       and_47_out, and_48_out, and_49_out, and_50_out, and_51_out, and_52_out, and_53_out, and_54_out,
       and_55_out, and_56_out, and_57_out, and_58_out, and_59_out, and_60_out, and_61_out, and_62_out,
       and_63_out, and_64_out, and_65_out, and_66_out, and_67_out, and_68_out, and_69_out, and_70_out,
       and_71_out, and_72_out, and_73_out, and_74_out, and_75_out, and_76_out, and_77_out, and_78_out,
       and_79_out, and_80_out, and_81_out, and_82_out, and_83_out, and_84_out, and_85_out, and_86_out,
       and_87_out, and_88_out, and_89_out, and_90_out, and_91_out, and_92_out, and_93_out, and_94_out,
       and_95_out, and_96_out, and_97_out, and_98_out, and_99_out, and_100_out, and_101_out, and_102_out,
       and_103_out, and_104_out, not_1_out, not_2_out, not_3_out, not_4_out, not_5_out, not_6_out, not_7_out,
       not_8_out, not_9_out, not_10_out, not_11_out, not_12_out, not_13_out, not_14_out, not_15_out;

  not not_1 (not_1_out, FLGs[3]);
  not not_2 (not_2_out, FLGs[2]);
  not not_3 (not_3_out, FLGs[0]);
  not not_4 (not_4_out, OPcode[7]);
  not not_5 (not_5_out, OPcode[6]);
  not not_6 (not_6_out, OPcode[5]);
  not not_7 (not_7_out, OPcode[4]);
  not not_8 (not_8_out, OPcode[3]);
  not not_9 (not_9_out, OPcode[2]);
  not not_10 (not_10_out, OPcode[1]);
  not not_11 (not_11_out, OPcode[0]);
  not not_12 (not_12_out, Steps[3]);
  not not_13 (not_13_out, Steps[2]);
  not not_14 (not_14_out, Steps[1]);
  not not_15 (not_15_out, Steps[0]);
  and and_1 (x[35], not_1_out, not_4_out, not_5_out, not_6_out, not_7_out, not_8_out, OPcode[2], OPcode[1], not_11_out, not_12_out, not_13_out, Steps[1], not_15_out);
  and and_2 (and_2_out, not_1_out, not_4_out, not_5_out, not_6_out, not_7_out, OPcode[3], not_9_out, OPcode[1], not_11_out, not_12_out, Steps[2], Steps[1], Steps[0]);
  and and_3 (and_3_out, not_1_out, not_4_out, not_5_out, not_6_out, not_7_out, OPcode[3], not_9_out, OPcode[1], OPcode[0], not_12_out, Steps[2], not_14_out, not_15_out);
  and and_4 (and_4_out, not_1_out, not_4_out, not_5_out, not_6_out, not_7_out, not_8_out, not_9_out, not_10_out, OPcode[0], Steps[3], not_13_out, Steps[1], not_15_out);
  and and_5 (x[33], not_1_out, not_4_out, not_5_out, not_6_out, not_7_out, OPcode[3], OPcode[2], not_10_out, not_11_out, not_12_out, Steps[2], Steps[1], Steps[0]);
  and and_6 (x[31], not_1_out, not_4_out, not_5_out, not_6_out, not_7_out, not_8_out, not_9_out, not_10_out, OPcode[0], Steps[3], not_13_out, Steps[1], not_15_out);
  and and_7 (x[30], not_1_out, not_4_out, not_5_out, not_6_out, not_7_out, not_8_out, not_9_out, not_10_out, OPcode[0], Steps[3], not_13_out, not_14_out, Steps[0]);
  and and_8 (and_8_out, not_1_out, not_4_out, not_5_out, not_6_out, not_7_out, not_8_out, OPcode[2], not_10_out, not_11_out, not_12_out, not_13_out, Steps[1], Steps[0]);
  and and_9 (and_9_out, not_1_out, not_4_out, not_5_out, not_6_out, not_7_out, OPcode[3], OPcode[2], not_10_out, not_11_out, not_12_out, Steps[2], Steps[1], Steps[0]);
  and and_10 (and_10_out, not_1_out, not_4_out, not_5_out, not_6_out, not_7_out, not_9_out, OPcode[0], not_12_out, not_13_out, Steps[0]);
  and and_11 (and_11_out, not_1_out, not_4_out, not_5_out, not_6_out, not_7_out, not_8_out, not_9_out, not_10_out, OPcode[0], not_13_out, not_14_out, Steps[0]);
  and and_12 (and_12_out, not_1_out, FLGs[2], not_4_out, not_5_out, not_6_out, not_7_out, not_9_out, OPcode[1], not_12_out, not_13_out, Steps[0]);
  and and_13 (and_13_out, not_1_out, not_4_out, not_5_out, not_6_out, not_7_out, not_8_out, not_12_out, not_13_out, not_14_out, Steps[0]);
  and and_14 (and_14_out, not_1_out, not_4_out, not_5_out, not_6_out, not_7_out, not_8_out, OPcode[1], OPcode[0], not_12_out, not_13_out, Steps[0]);
  and and_15 (and_15_out, not_1_out, not_4_out, not_5_out, not_6_out, not_7_out, not_8_out, OPcode[1], OPcode[0], not_12_out, not_14_out, Steps[0]);
  and and_16 (and_16_out, not_1_out, not_4_out, not_5_out, not_6_out, not_7_out, OPcode[3], not_9_out, not_10_out, OPcode[0], not_12_out, Steps[0]);
  and and_17 (and_17_out, not_1_out, not_4_out, not_5_out, not_6_out, not_7_out, OPcode[3], not_9_out, OPcode[1], not_11_out, not_12_out, Steps[0]);
  and and_18 (and_18_out, not_1_out, not_4_out, not_5_out, not_6_out, not_7_out, OPcode[3], OPcode[2], not_10_out, not_11_out, not_12_out, not_13_out, Steps[0]);
  and and_19 (and_19_out, not_1_out, not_4_out, not_5_out, not_6_out, not_7_out, OPcode[3], OPcode[2], not_10_out, not_11_out, not_12_out, not_14_out, Steps[0]);
  and and_20 (and_20_out, not_1_out, not_4_out, not_5_out, not_6_out, not_7_out, not_9_out, not_10_out, OPcode[0], not_12_out, not_14_out, Steps[0]);
  and and_21 (and_21_out, not_1_out, FLGs[2], not_4_out, not_5_out, not_6_out, not_7_out, not_9_out, OPcode[1], not_11_out, not_12_out, not_14_out, Steps[0]);
  and and_22 (and_22_out, not_1_out, not_4_out, not_5_out, not_6_out, not_7_out, not_10_out, not_11_out, not_12_out, not_13_out, not_14_out, Steps[0]);
  and and_23 (and_23_out, not_1_out, FLGs[0], not_4_out, not_5_out, not_6_out, not_7_out, OPcode[3], not_10_out, not_11_out, not_12_out, not_13_out, Steps[0]);
  and and_24 (and_24_out, not_1_out, FLGs[0], not_4_out, not_5_out, not_6_out, not_7_out, OPcode[3], not_9_out, not_11_out, not_12_out, not_14_out, Steps[0]);
  and and_25 (and_25_out, not_1_out, not_4_out, not_5_out, not_6_out, not_7_out, OPcode[2], not_10_out, not_11_out, not_12_out, not_13_out, not_15_out);
  and and_26 (and_26_out, not_1_out, not_4_out, not_5_out, not_6_out, not_7_out, not_8_out, not_12_out, not_13_out, not_14_out, not_15_out);
  and and_27 (and_27_out, not_1_out, not_4_out, not_5_out, not_6_out, not_7_out, not_8_out, OPcode[1], OPcode[0], not_12_out, not_15_out);
  and and_28 (and_28_out, not_1_out, not_4_out, not_5_out, not_6_out, not_7_out, not_9_out, not_10_out, OPcode[0], not_12_out, not_15_out);
  and and_29 (and_29_out, not_1_out, not_4_out, not_5_out, not_6_out, not_7_out, OPcode[3], not_9_out, OPcode[1], not_11_out, not_12_out, not_15_out);
  and and_30 (and_30_out, not_1_out, not_4_out, not_5_out, not_6_out, not_7_out, OPcode[3], OPcode[2], not_10_out, not_11_out, not_12_out, not_15_out);
  and and_31 (and_31_out, not_1_out, not_4_out, not_5_out, not_6_out, not_7_out, not_9_out, not_12_out, not_13_out, not_14_out, not_15_out);
  and and_32 (and_32_out, not_1_out, FLGs[2], not_4_out, not_5_out, not_6_out, not_7_out, not_9_out, OPcode[1], not_11_out, not_12_out, not_15_out);
  and and_33 (and_33_out, not_1_out, FLGs[0], not_4_out, not_5_out, not_6_out, not_7_out, OPcode[3], not_10_out, not_11_out, not_12_out, not_15_out);
  and and_34 (and_34_out, not_1_out, not_4_out, not_5_out, not_6_out, not_7_out, OPcode[3], not_9_out, OPcode[1], not_12_out, not_13_out, not_15_out);
  and and_35 (and_35_out, not_1_out, not_4_out, not_5_out, not_6_out, not_7_out, not_8_out, not_12_out, not_13_out, not_14_out, Steps[0]);
  and and_36 (and_36_out, not_1_out, not_4_out, not_5_out, not_6_out, not_7_out, not_9_out, not_12_out, not_13_out, not_14_out, Steps[0]);
  and and_37 (and_37_out, not_1_out, not_4_out, not_5_out, not_6_out, not_7_out, not_10_out, not_11_out, not_12_out, not_13_out, not_14_out, Steps[0]);
  and and_38 (and_38_out, not_1_out, FLGs[0], not_4_out, not_5_out, not_6_out, not_7_out, OPcode[3], not_9_out, not_11_out, Steps[3], not_13_out, not_14_out, not_15_out);
  and and_39 (and_39_out, not_1_out, not_4_out, not_5_out, not_6_out, not_7_out, not_8_out, not_9_out, not_10_out, OPcode[0], Steps[3], not_13_out, not_14_out, not_15_out);
  and and_40 (and_40_out, not_1_out, not_4_out, not_5_out, not_6_out, not_7_out, OPcode[3], not_9_out, OPcode[1], not_11_out, Steps[3], not_13_out, not_14_out, not_15_out);
  and and_41 (and_41_out, not_1_out, not_4_out, not_5_out, not_6_out, not_7_out, OPcode[3], not_9_out, OPcode[1], OPcode[0], not_12_out, Steps[2], not_14_out, Steps[0]);
  and and_42 (x[19], not_1_out, not_4_out, not_5_out, not_6_out, not_7_out, OPcode[3], not_9_out, not_10_out, OPcode[0], not_12_out, Steps[2], Steps[1], Steps[0]);
  and and_43 (and_43_out, not_1_out, not_4_out, not_5_out, not_6_out, not_7_out, not_9_out, OPcode[0], not_12_out, not_13_out, Steps[0]);
  and and_44 (and_44_out, not_1_out, not_2_out, not_4_out, not_5_out, not_6_out, not_7_out, not_8_out, not_9_out, OPcode[1], not_11_out, not_12_out, not_13_out, Steps[1]);
  and and_45 (and_45_out, not_1_out, not_4_out, not_5_out, not_6_out, not_7_out, not_9_out, OPcode[1], not_12_out, not_13_out, Steps[0]);
  and and_46 (and_46_out, not_1_out, not_4_out, not_5_out, not_6_out, not_7_out, not_8_out, not_12_out, not_13_out, not_14_out, Steps[0]);
  and and_47 (and_47_out, not_1_out, not_4_out, not_5_out, not_6_out, not_7_out, not_8_out, OPcode[1], OPcode[0], not_12_out, not_13_out, Steps[0]);
  and and_48 (and_48_out, not_1_out, not_4_out, not_5_out, not_6_out, not_7_out, not_8_out, OPcode[1], OPcode[0], not_12_out, not_14_out, Steps[0]);
  and and_49 (and_49_out, not_1_out, not_3_out, not_4_out, not_5_out, not_6_out, not_7_out, OPcode[3], not_9_out, not_10_out, not_11_out, not_12_out, not_13_out, Steps[1]);
  and and_50 (and_50_out, not_1_out, not_4_out, not_5_out, not_6_out, not_7_out, not_9_out, not_10_out, OPcode[0], not_12_out, not_14_out, Steps[0]);
  and and_51 (and_51_out, not_1_out, not_4_out, not_5_out, not_6_out, not_7_out, OPcode[3], not_9_out, OPcode[1], not_11_out, not_12_out, not_14_out, Steps[0]);
  and and_52 (and_52_out, not_1_out, not_4_out, not_5_out, not_6_out, not_7_out, OPcode[3], not_10_out, not_11_out, not_12_out, not_13_out, Steps[0]);
  and and_53 (and_53_out, not_1_out, not_4_out, not_5_out, not_6_out, not_7_out, OPcode[3], OPcode[2], not_10_out, not_11_out, not_12_out, not_14_out, Steps[0]);
  and and_54 (and_54_out, not_1_out, FLGs[2], not_4_out, not_5_out, not_6_out, not_7_out, not_9_out, OPcode[1], not_11_out, not_12_out, not_14_out, Steps[0]);
  and and_55 (and_55_out, not_1_out, FLGs[0], not_4_out, not_5_out, not_6_out, not_7_out, OPcode[3], not_9_out, not_11_out, not_12_out, not_14_out, Steps[0]);
  and and_56 (and_56_out, not_1_out, not_4_out, not_5_out, not_6_out, not_7_out, not_9_out, OPcode[0], not_12_out, not_13_out, not_15_out);
  and and_57 (and_57_out, not_1_out, FLGs[2], not_4_out, not_5_out, not_6_out, not_7_out, not_9_out, OPcode[1], not_12_out, not_13_out, not_15_out);
  and and_58 (and_58_out, not_1_out, not_4_out, not_5_out, not_6_out, not_7_out, not_8_out, not_12_out, not_13_out, not_14_out, not_15_out);
  and and_59 (and_59_out, not_1_out, not_4_out, not_5_out, not_6_out, not_7_out, not_8_out, OPcode[1], OPcode[0], not_12_out, not_13_out, not_15_out);
  and and_60 (and_60_out, not_1_out, not_4_out, not_5_out, not_6_out, not_7_out, not_8_out, OPcode[1], OPcode[0], not_12_out, not_14_out, not_15_out);
  and and_61 (and_61_out, not_1_out, not_4_out, not_5_out, not_6_out, not_7_out, not_9_out, not_10_out, OPcode[0], not_12_out, not_14_out, not_15_out);
  and and_62 (and_62_out, not_1_out, not_4_out, not_5_out, not_6_out, not_7_out, OPcode[3], not_9_out, OPcode[1], not_12_out, not_13_out, not_15_out);
  and and_63 (and_63_out, not_1_out, not_4_out, not_5_out, not_6_out, not_7_out, OPcode[3], not_9_out, OPcode[1], not_11_out, not_12_out, not_14_out, not_15_out);
  and and_64 (and_64_out, not_1_out, not_4_out, not_5_out, not_6_out, not_7_out, OPcode[3], OPcode[2], not_10_out, not_11_out, not_12_out, not_13_out, not_15_out);
  and and_65 (and_65_out, not_1_out, not_4_out, not_5_out, not_6_out, not_7_out, OPcode[3], OPcode[2], not_10_out, not_11_out, not_12_out, not_14_out, not_15_out);
  and and_66 (and_66_out, not_1_out, FLGs[2], not_4_out, not_5_out, not_6_out, not_7_out, not_9_out, OPcode[1], not_11_out, not_12_out, not_14_out, not_15_out);
  and and_67 (and_67_out, not_1_out, not_4_out, not_5_out, not_6_out, not_7_out, not_10_out, not_11_out, not_12_out, not_13_out, not_14_out, not_15_out);
  and and_68 (and_68_out, not_1_out, FLGs[0], not_4_out, not_5_out, not_6_out, not_7_out, OPcode[3], not_10_out, not_11_out, not_12_out, not_13_out, not_15_out);
  and and_69 (and_69_out, not_1_out, FLGs[0], not_4_out, not_5_out, not_6_out, not_7_out, OPcode[3], not_9_out, not_11_out, not_12_out, not_14_out, not_15_out);
  and and_70 (and_70_out, not_1_out, FLGs[0], not_4_out, not_5_out, not_6_out, not_7_out, OPcode[3], not_9_out, not_10_out, not_11_out, not_12_out, Steps[2], Steps[1], Steps[0]);
  and and_71 (and_71_out, not_1_out, FLGs[2], not_4_out, not_5_out, not_6_out, not_7_out, not_8_out, not_9_out, OPcode[1], not_11_out, not_12_out, Steps[2], Steps[1], Steps[0]);
  and and_72 (and_72_out, not_1_out, not_4_out, not_5_out, not_6_out, not_7_out, not_8_out, OPcode[2], OPcode[1], OPcode[0], not_12_out, Steps[2], Steps[1], Steps[0]);
  and and_73 (and_73_out, not_1_out, not_4_out, not_5_out, not_6_out, not_7_out, not_9_out, not_10_out, OPcode[0], not_12_out, not_13_out, Steps[1], Steps[0]);
  and and_74 (and_74_out, not_1_out, not_4_out, not_5_out, not_6_out, not_7_out, OPcode[3], not_9_out, OPcode[1], not_11_out, not_12_out, not_13_out, Steps[1], Steps[0]);
  and and_75 (and_75_out, not_1_out, not_4_out, not_5_out, not_6_out, not_7_out, OPcode[3], OPcode[2], not_10_out, not_11_out, not_12_out, not_13_out, Steps[1], Steps[0]);
  and and_76 (and_76_out, not_1_out, not_4_out, not_5_out, not_6_out, not_7_out, not_8_out, OPcode[1], OPcode[0], not_12_out, not_13_out, Steps[1], Steps[0]);
  and and_77 (and_77_out, not_1_out, FLGs[0], not_4_out, not_5_out, not_6_out, not_7_out, OPcode[3], not_10_out, not_11_out, not_12_out, not_13_out, Steps[1], Steps[0]);
  and and_78 (and_78_out, not_1_out, FLGs[2], not_4_out, not_5_out, not_6_out, not_7_out, not_9_out, OPcode[1], not_11_out, not_12_out, not_13_out, Steps[1], Steps[0]);
  and and_79 (and_79_out, not_1_out, not_4_out, not_5_out, not_6_out, not_7_out, not_9_out, not_10_out, OPcode[0], not_12_out, Steps[2], not_14_out, Steps[0]);
  and and_80 (and_80_out, not_1_out, not_4_out, not_5_out, not_6_out, not_7_out, OPcode[3], not_9_out, OPcode[1], not_11_out, not_12_out, Steps[2], not_14_out, Steps[0]);
  and and_81 (and_81_out, not_1_out, not_4_out, not_5_out, not_6_out, not_7_out, OPcode[3], OPcode[2], not_10_out, not_11_out, not_12_out, Steps[2], not_14_out, Steps[0]);
  and and_82 (and_82_out, not_1_out, not_4_out, not_5_out, not_6_out, not_7_out, not_8_out, OPcode[1], OPcode[0], not_12_out, Steps[2], not_14_out, Steps[0]);
  and and_83 (and_83_out, not_1_out, FLGs[0], not_4_out, not_5_out, not_6_out, not_7_out, OPcode[3], not_10_out, not_11_out, not_12_out, Steps[2], not_14_out, Steps[0]);
  and and_84 (and_84_out, not_1_out, FLGs[2], not_4_out, not_5_out, not_6_out, not_7_out, not_9_out, OPcode[1], not_11_out, not_12_out, Steps[2], not_14_out, Steps[0]);
  and and_85 (and_85_out, not_1_out, FLGs[0], not_4_out, not_5_out, not_6_out, not_7_out, OPcode[3], not_9_out, not_10_out, not_11_out, not_12_out, Steps[2], Steps[1]);
  and and_86 (and_86_out, not_1_out, not_4_out, not_5_out, not_6_out, not_7_out, not_9_out, not_10_out, OPcode[0], not_12_out, Steps[2], Steps[1], not_15_out);
  and and_87 (and_87_out, not_1_out, not_4_out, not_5_out, not_6_out, not_7_out, OPcode[3], not_9_out, OPcode[1], not_11_out, not_12_out, Steps[2], Steps[1], not_15_out);
  and and_88 (and_88_out, not_1_out, FLGs[2], not_4_out, not_5_out, not_6_out, not_7_out, not_8_out, not_9_out, OPcode[1], not_12_out, Steps[2], Steps[1]);
  and and_89 (and_89_out, not_1_out, not_4_out, not_5_out, not_6_out, not_7_out, not_8_out, OPcode[1], OPcode[0], not_12_out, Steps[2], Steps[1]);
  and and_90 (and_90_out, not_1_out, not_4_out, not_5_out, not_6_out, not_7_out, OPcode[3], OPcode[2], not_10_out, not_11_out, not_12_out, Steps[2], Steps[1], not_15_out);
  and and_91 (and_91_out, not_1_out, not_4_out, not_5_out, not_6_out, not_7_out, not_8_out, not_9_out, not_10_out, not_11_out, not_12_out, not_13_out, Steps[1], not_15_out);
  and and_92 (and_92_out, not_1_out, not_4_out, not_5_out, not_6_out, not_7_out, not_8_out, not_9_out, not_10_out, OPcode[0], Steps[3], not_13_out, Steps[1], Steps[0]);
  and and_93 (and_93_out, not_1_out, not_2_out, not_4_out, not_5_out, not_6_out, not_7_out, not_8_out, not_9_out, OPcode[1], not_11_out, not_12_out, Steps[2], not_14_out, not_15_out);
  and and_94 (and_94_out, not_1_out, FLGs[2], not_4_out, not_5_out, not_6_out, not_7_out, not_8_out, not_9_out, OPcode[1], Steps[3], not_13_out, not_14_out, not_15_out);
  and and_95 (and_95_out, not_1_out, not_4_out, not_5_out, not_6_out, not_7_out, not_8_out, OPcode[1], OPcode[0], Steps[3], not_13_out, not_14_out, not_15_out);
  and and_96 (and_96_out, not_1_out, not_4_out, not_5_out, not_6_out, not_7_out, not_8_out, OPcode[2], not_10_out, not_11_out, not_12_out, Steps[2], not_14_out, not_15_out);
  and and_97 (and_97_out, not_1_out, not_4_out, not_5_out, not_6_out, not_7_out, not_8_out, OPcode[2], not_10_out, OPcode[0], not_12_out, not_13_out, Steps[1], Steps[0]);
  and and_98 (and_98_out, not_1_out, not_4_out, not_5_out, not_6_out, not_7_out, not_8_out, OPcode[2], OPcode[1], not_11_out, not_12_out, not_13_out, Steps[1], Steps[0]);
  and and_99 (and_99_out, not_1_out, not_3_out, not_4_out, not_5_out, not_6_out, not_7_out, OPcode[3], not_9_out, not_10_out, not_11_out, not_12_out, Steps[2], not_14_out, not_15_out);
  and and_100 (and_100_out, not_1_out, FLGs[0], not_4_out, not_5_out, not_6_out, not_7_out, OPcode[3], not_9_out, not_11_out, Steps[3], not_13_out, not_14_out, Steps[0]);
  and and_101 (and_101_out, not_1_out, not_4_out, not_5_out, not_6_out, not_7_out, OPcode[3], not_9_out, not_10_out, OPcode[0], Steps[3], not_13_out, not_14_out, not_15_out);
  and and_102 (and_102_out, not_1_out, not_4_out, not_5_out, not_6_out, not_7_out, OPcode[3], not_9_out, OPcode[1], not_11_out, Steps[3], not_13_out, not_14_out, Steps[0]);
  and and_103 (and_103_out, not_1_out, not_4_out, not_5_out, not_6_out, not_7_out, OPcode[3], not_9_out, OPcode[1], OPcode[0], not_12_out, Steps[2], Steps[1], not_15_out);
  and and_104 (and_104_out, not_1_out, not_4_out, not_5_out, not_6_out, not_7_out, OPcode[3], OPcode[2], not_10_out, not_11_out, Steps[3], not_13_out, not_14_out, not_15_out);
  and and_105 (x[9], not_1_out, not_4_out, not_5_out, not_6_out, not_7_out, OPcode[3], not_9_out, OPcode[1], OPcode[0], not_12_out, not_13_out, Steps[1], Steps[0]);
  and and_106 (x[8], not_1_out, not_4_out, not_5_out, not_6_out, not_7_out, OPcode[3], not_9_out, OPcode[1], OPcode[0], not_12_out, Steps[2], not_14_out, not_15_out);
  and and_107 (x[7], not_1_out, not_4_out, not_5_out, not_6_out, not_7_out, not_8_out, not_9_out, OPcode[1], OPcode[0], not_12_out, Steps[2], Steps[1], Steps[0]);
  and and_108 (x[5], not_1_out, not_4_out, not_5_out, not_6_out, not_7_out, not_8_out, OPcode[2], not_10_out, OPcode[0], not_12_out, not_13_out, Steps[1], not_15_out);
  and and_109 (x[4], not_1_out, not_4_out, not_5_out, not_6_out, not_7_out, not_8_out, OPcode[2], not_10_out, not_11_out, not_12_out, not_13_out, Steps[1], not_15_out);
  and and_110 (x[3], not_1_out, not_4_out, not_5_out, not_6_out, not_7_out, not_8_out, OPcode[2], not_10_out, not_11_out, not_12_out, not_13_out, Steps[1], Steps[0]);
  and and_111 (x[2], not_1_out, not_4_out, not_5_out, not_6_out, not_7_out, not_8_out, not_9_out, not_10_out, OPcode[0], not_12_out, Steps[2], Steps[1], Steps[0]);
  or or_1 (x[34], and_2_out, and_3_out, and_4_out);
  or or_2 (x[24], and_8_out, and_9_out);
  or or_3 (x[22], and_25_out, and_26_out, and_27_out, and_28_out, and_29_out, and_30_out, and_31_out, and_32_out, and_33_out, and_34_out);
  or or_4 (x[21], and_35_out, and_36_out, and_37_out);
  or or_5 (x[20], and_38_out, and_39_out, and_40_out, and_41_out);
  or or_6 (x[18], and_43_out, and_44_out, and_45_out, and_46_out, and_47_out, and_48_out, and_49_out, and_50_out, and_51_out, and_52_out, and_53_out, and_54_out, and_55_out);
  or or_7 (x[16], and_70_out, and_71_out, and_72_out);
  or or_8 (x[13], and_73_out, and_74_out, and_75_out, and_76_out, and_77_out, and_78_out);
  or or_9 (x[12], and_79_out, and_80_out, and_81_out, and_82_out, and_83_out, and_84_out);
  or or_10 (x[11], and_85_out, and_86_out, and_87_out, and_88_out, and_89_out, and_90_out);
  or or_11 (x[23], and_10_out, and_11_out, and_12_out, and_13_out, and_14_out, and_15_out, and_16_out, and_17_out, and_18_out, and_19_out, and_20_out, and_21_out, and_22_out, and_23_out, and_24_out);
  or or_12 (x[17], and_56_out, and_57_out, and_58_out, and_59_out, and_60_out, and_61_out, and_62_out, and_63_out, and_64_out, and_65_out, and_66_out, and_67_out, and_68_out, and_69_out);
  or or_13 (x[10], and_91_out, and_92_out, and_93_out, and_94_out, and_95_out, and_96_out, and_97_out, and_98_out, and_99_out, and_100_out, and_101_out, and_102_out, and_103_out, and_104_out);

  assign {x[32], x[29:25], x[15:14], x[6], x[1:0]} = {11{1'b0}};
endmodule

module testes (
  input  [3:0] FLGs,
  input  [7:0] OPcode,
  input  [3:0] Steps,
  output [35:0] out_4
);

  ROM #(.addrWidth(16), .dataWidth(36)) rom_1 (.addr({FLGs, OPcode, Steps}), .data(out_4));

  // Notes on the sheet:
  //   contents of rom_1 (hex, n*v repeats v):
  //   420000 a40000 400 13*0 420000 a40000 420000 842000 420000 841000 400800 4 100000 40800000 480000000
  //   400 4*0 420000 a40000 40000 40000 400 11*0 420000 a40000 420000 842000 420000 841000 400800 880 400
  //   7*0 420000 a40000 400010 1000008 400 11*0 420000 a40000 20 400 12*0 420000 a40000 800000000 400 12*0
  //   420000 a40000 420000 842000 420000 841000 400800 10800 400 7*0 420000 a40000 40000 40000 400 11*0
  //   420000 a40000 420000 842000 420000 841000 400800 880000 400 7*0 420000 a40000 420000 842000 420000
  //   841000 400800 400800000 100000 400 6*0 420000 a40000 420000 840200 400000100 100000 400 9*0 420000
  //   a40000 420000 842000 420000 841000 400800 201000000 400 3895*0 420000 a40000 400 13*0 420000 a40000
  //   420000 842000 420000 841000 400800 4 100000 40800000 480000000 400 4*0 420000 a40000 40000 40000 400
  //   11*0 420000 a40000 420000 842000 420000 841000 400800 880 400 7*0 420000 a40000 400010 1000008 400
  //   11*0 420000 a40000 20 400 12*0 420000 a40000 800000000 400 12*0 420000 a40000 420000 842000 420000
  //   841000 400800 10800 400 7*0 420000 a40000 420000 842000 420000 841000 400800 10800 100000 400 6*0
  //   420000 a40000 420000 842000 420000 841000 400800 880000 400 7*0 420000 a40000 420000 842000 420000
  //   841000 400800 400800000 100000 400 6*0 420000 a40000 420000 840200 400000100 100000 400 9*0 420000
  //   a40000 420000 842000 420000 841000 400800 201000000 400 3895*0 420000 a40000 400 13*0 420000 a40000
  //   420000 842000 420000 841000 400800 4 100000 40800000 480000000 400 4*0 420000 a40000 40000 40000 400
  //   11*0 420000 a40000 420000 842000 420000 841000 400800 880 400 7*0 420000 a40000 400010 1000008 400
  //   11*0 420000 a40000 20 400 12*0 420000 a40000 800000000 400 12*0 420000 a40000 420000 842000 420000
  //   841000 400800 10800 400 7*0 420000 a40000 40000 40000 400 11*0 420000 a40000 420000 842000 420000
  //   841000 400800 880000 400 7*0 420000 a40000 420000 842000 420000 841000 400800 400800000 100000 400
  //   6*0 420000 a40000 420000 840200 400000100 100000 400 9*0 420000 a40000 420000 842000 420000 841000
  //   400800 201000000 400 3895*0 420000 a40000 400 13*0 420000 a40000 420000 842000 420000 841000 400800
  //   4 100000 40800000 480000000 400 4*0 420000 a40000 40000 40000 400 11*0 420000 a40000 420000 842000
  //   420000 841000 400800 880 400 7*0 420000 a40000 400010 1000008 400 11*0 420000 a40000 20 400 12*0
  //   420000 a40000 800000000 400 12*0 420000 a40000 420000 842000 420000 841000 400800 10800 400 7*0
  //   420000 a40000 420000 842000 420000 841000 400800 10800 100000 400 6*0 420000 a40000 420000 842000
  //   420000 841000 400800 880000 400 7*0 420000 a40000 420000 842000 420000 841000 400800 400800000
  //   100000 400 6*0 420000 a40000 420000 840200 400000100 100000 400 9*0 420000 a40000 420000 842000
  //   420000 841000 400800 201000000 400 3895*0 420000 a40000 400 13*0 420000 a40000 420000 842000 420000
  //   841000 400800 4 100000 40800000 480000000 400 4*0 420000 a40000 420000 842000 420000 841000 400800
  //   10800 400 7*0 420000 a40000 420000 842000 420000 841000 400800 880 400 7*0 420000 a40000 400010
  //   1000008 400 11*0 420000 a40000 20 400 12*0 420000 a40000 800000000 400 12*0 420000 a40000 420000
  //   842000 420000 841000 400800 10800 400 7*0 420000 a40000 40000 40000 400 11*0 420000 a40000 420000
  //   842000 420000 841000 400800 880000 400 7*0 420000 a40000 420000 842000 420000 841000 400800
  //   400800000 100000 400 6*0 420000 a40000 420000 840200 400000100 100000 400 9*0 420000 a40000 420000
  //   842000 420000 841000 400800 201000000 400 3895*0 420000 a40000 400 13*0 420000 a40000 420000 842000
  //   420000 841000 400800 4 100000 40800000 480000000 400 4*0 420000 a40000 420000 842000 420000 841000
  //   400800 10800 400 7*0 420000 a40000 420000 842000 420000 841000 400800 880 400 7*0 420000 a40000
  //   400010 1000008 400 11*0 420000 a40000 20 400 12*0 420000 a40000 800000000 400 12*0 420000 a40000
  //   420000 842000 420000 841000 400800 10800 400 7*0 420000 a40000 420000 842000 420000 841000 400800
  //   10800 100000 400 6*0 420000 a40000 420000 842000 420000 841000 400800 880000 400 7*0 420000 a40000
  //   420000 842000 420000 841000 400800 400800000 100000 400 6*0 42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
endmodule

module testess (
  input  [7:0] in_1,
  output [7:0] out_2
);

  ROM rom_1 (.addr(in_1), .data(out_2));
endmodule

module Selector (
  input  Slct,
  input  A,
  input  B,
  output AorB,
  output out_5
);

  wire and_1_out, and_2_out;

  and and_1 (and_1_out, A, ~Slct);  // AND_Gate
  and and_2 (and_2_out, B, Slct);
  or or_1 (AorB, and_1_out, and_2_out);

  assign out_5 = Slct;
endmodule

module Selector_8_bits (
  input  in_1,
  input  [7:0] in_2,
  input  [7:0] in_3,
  output [7:0] out_4
);

  wire selector_1_out_5, selector_2_out_5, selector_3_out_5, selector_4_out_5, selector_5_out_5,
       selector_6_out_5, selector_7_out_5;

  Selector selector_1 (.B(in_3[0]), .A(in_2[0]), .Slct(in_1), .out_5(selector_1_out_5), .AorB(out_4[0]));
  Selector selector_2 (.B(in_3[1]), .A(in_2[1]), .Slct(selector_1_out_5), .out_5(selector_2_out_5), .AorB(out_4[1]));
  Selector selector_3 (.B(in_3[2]), .A(in_2[2]), .Slct(selector_2_out_5), .out_5(selector_3_out_5), .AorB(out_4[2]));
  Selector selector_4 (.B(in_3[3]), .A(in_2[3]), .Slct(selector_3_out_5), .out_5(selector_4_out_5), .AorB(out_4[3]));
  Selector selector_5 (.B(in_3[4]), .A(in_2[4]), .Slct(selector_4_out_5), .out_5(selector_5_out_5), .AorB(out_4[4]));
  Selector selector_6 (.B(in_3[5]), .A(in_2[5]), .Slct(selector_5_out_5), .out_5(selector_6_out_5), .AorB(out_4[5]));
  Selector selector_7 (.B(in_3[6]), .A(in_2[6]), .Slct(selector_6_out_5), .out_5(selector_7_out_5), .AorB(out_4[6]));
  Selector selector_8 (.B(in_3[7]), .A(in_2[7]), .Slct(selector_7_out_5), .AorB(out_4[7]));  // open: out_5
endmodule

module Selector_24_bits (
  input  in_1,
  input  [23:0] in_2,
  input  [23:0] in_3,
  output [23:0] out_4
);

  wire selector_1_out_5, selector_2_out_5, selector_3_out_5, selector_4_out_5, selector_5_out_5,
       selector_6_out_5, selector_7_out_5, selector_8_out_5, selector_9_out_5, selector_10_out_5,
       selector_11_out_5, selector_12_out_5, selector_13_out_5, selector_14_out_5, selector_15_out_5,
       selector_16_out_5, selector_17_out_5, selector_18_out_5, selector_19_out_5, selector_20_out_5,
       selector_21_out_5, selector_22_out_5, selector_23_out_5;

  Selector selector_1 (.B(in_3[0]), .A(in_2[0]), .Slct(in_1), .out_5(selector_1_out_5), .AorB(out_4[0]));
  Selector selector_2 (.B(in_3[1]), .A(in_2[1]), .Slct(selector_1_out_5), .out_5(selector_2_out_5), .AorB(out_4[1]));
  Selector selector_3 (.B(in_3[2]), .A(in_2[2]), .Slct(selector_2_out_5), .out_5(selector_3_out_5), .AorB(out_4[2]));
  Selector selector_4 (.B(in_3[3]), .A(in_2[3]), .Slct(selector_3_out_5), .out_5(selector_4_out_5), .AorB(out_4[3]));
  Selector selector_5 (.B(in_3[4]), .A(in_2[4]), .Slct(selector_4_out_5), .out_5(selector_5_out_5), .AorB(out_4[4]));
  Selector selector_6 (.B(in_3[5]), .A(in_2[5]), .Slct(selector_5_out_5), .out_5(selector_6_out_5), .AorB(out_4[5]));
  Selector selector_7 (.B(in_3[6]), .A(in_2[6]), .Slct(selector_6_out_5), .out_5(selector_7_out_5), .AorB(out_4[6]));
  Selector selector_8 (.B(in_3[7]), .A(in_2[7]), .Slct(selector_7_out_5), .out_5(selector_8_out_5), .AorB(out_4[7]));
  Selector selector_9 (.B(in_3[8]), .A(in_2[8]), .Slct(selector_8_out_5), .out_5(selector_9_out_5), .AorB(out_4[8]));
  Selector selector_10 (.B(in_3[9]), .A(in_2[9]), .Slct(selector_9_out_5), .out_5(selector_10_out_5), .AorB(out_4[9]));
  Selector selector_11 (
    .B(in_3[10]), .A(in_2[10]), .Slct(selector_10_out_5), .out_5(selector_11_out_5), .AorB(out_4[10]));
  Selector selector_12 (
    .B(in_3[11]), .A(in_2[11]), .Slct(selector_11_out_5), .out_5(selector_12_out_5), .AorB(out_4[11]));
  Selector selector_13 (
    .B(in_3[12]), .A(in_2[12]), .Slct(selector_12_out_5), .out_5(selector_13_out_5), .AorB(out_4[12]));
  Selector selector_14 (
    .B(in_3[13]), .A(in_2[13]), .Slct(selector_13_out_5), .out_5(selector_14_out_5), .AorB(out_4[13]));
  Selector selector_15 (
    .B(in_3[14]), .A(in_2[14]), .Slct(selector_14_out_5), .out_5(selector_15_out_5), .AorB(out_4[14]));
  Selector selector_16 (
    .B(in_3[15]), .A(in_2[15]), .Slct(selector_15_out_5), .out_5(selector_16_out_5), .AorB(out_4[15]));
  Selector selector_17 (
    .B(in_3[16]), .A(in_2[16]), .Slct(selector_16_out_5), .out_5(selector_17_out_5), .AorB(out_4[16]));
  Selector selector_18 (
    .B(in_3[17]), .A(in_2[17]), .Slct(selector_17_out_5), .out_5(selector_18_out_5), .AorB(out_4[17]));
  Selector selector_19 (
    .B(in_3[18]), .A(in_2[18]), .Slct(selector_18_out_5), .out_5(selector_19_out_5), .AorB(out_4[18]));
  Selector selector_20 (
    .B(in_3[19]), .A(in_2[19]), .Slct(selector_19_out_5), .out_5(selector_20_out_5), .AorB(out_4[19]));
  Selector selector_21 (
    .B(in_3[20]), .A(in_2[20]), .Slct(selector_20_out_5), .out_5(selector_21_out_5), .AorB(out_4[20]));
  Selector selector_22 (
    .B(in_3[21]), .A(in_2[21]), .Slct(selector_21_out_5), .out_5(selector_22_out_5), .AorB(out_4[21]));
  Selector selector_23 (
    .B(in_3[22]), .A(in_2[22]), .Slct(selector_22_out_5), .out_5(selector_23_out_5), .AorB(out_4[22]));
  Selector selector_24 (.B(in_3[23]), .A(in_2[23]), .Slct(selector_23_out_5), .AorB(out_4[23]));  // open: out_5
endmodule
