// Logisim project conttrol_unit.circ as structural Verilog: 5 circuits, main circuit Conttrol
module Conttrol (
  input  [3:0] FLGs,
  input  [7:0] OPcode,
  input  [3:0] Steps,
  output [35:0] out_4
);

  ROM #(.addrWidth(16), .dataWidth(36)) rom_1 (.addr({FLGs, OPcode, Steps}), .data(out_4));

  // Notes on the sheet:
  //   contents of rom_1 (hex, n*v repeats v):
  //   4200 a400 4200 8420 4200 8410 4008 408000 4800000 4 6*0 4200 a400 4200 8420 4200 8410 4008 8100 4
  //   4071*0 4200 a400 408000 4800000 4 11*0 4200 a400 4200 8420 4200 8410 4008 8100 4 4071*0 4200 a400
  //   408000 4800000 4 11*0 4200 a400 4200 8420 4200 8410 4008 8100 4 4071*0 4200 a400 408000 4800000 4
  //   11*0 4200 a400 4200 8420 4200 8410 4008 8100 4
endmodule

module selector (
  input  A,
  input  B,
  input  Slct,
  output AorB
);

  wire and_1_out, and_2_out;

  and and_1 (and_1_out, A, ~Slct);  // AND_Gate
  and and_2 (and_2_out, B, Slct);
  or or_1 (AorB, and_1_out, and_2_out);
endmodule

module selectoor (
  input  [15:0] in_1,
  input  [15:0] in_2,
  input  slct,
  output [15:0] out_4
);

  selector selector_1 (.B(in_2[0]), .A(in_1[0]), .Slct(slct), .AorB(out_4[0]));
  selector selector_2 (.B(in_2[1]), .A(in_1[1]), .Slct(slct), .AorB(out_4[1]));
  selector selector_3 (.B(in_2[2]), .A(in_1[2]), .Slct(slct), .AorB(out_4[2]));
  selector selector_4 (.B(in_2[3]), .A(in_1[3]), .Slct(slct), .AorB(out_4[3]));
  selector selector_5 (.B(in_2[4]), .A(in_1[4]), .Slct(slct), .AorB(out_4[4]));
  selector selector_6 (.B(in_2[5]), .A(in_1[5]), .Slct(slct), .AorB(out_4[5]));
  selector selector_7 (.B(in_2[6]), .A(in_1[6]), .Slct(slct), .AorB(out_4[6]));
  selector selector_8 (.B(in_2[7]), .A(in_1[7]), .Slct(slct), .AorB(out_4[7]));
  selector selector_9 (.B(in_2[8]), .A(in_1[8]), .Slct(slct), .AorB(out_4[8]));
  selector selector_10 (.B(in_2[9]), .A(in_1[9]), .Slct(slct), .AorB(out_4[9]));
  selector selector_11 (.B(in_2[10]), .A(in_1[10]), .Slct(slct), .AorB(out_4[10]));
  selector selector_12 (.B(in_2[11]), .A(in_1[11]), .Slct(slct), .AorB(out_4[11]));
  selector selector_13 (.B(in_2[12]), .A(in_1[12]), .Slct(slct), .AorB(out_4[12]));
  selector selector_14 (.B(in_2[13]), .A(in_1[13]), .Slct(slct), .AorB(out_4[13]));
  selector selector_15 (.B(in_2[14]), .A(in_1[14]), .Slct(slct), .AorB(out_4[14]));
  selector selector_16 (.B(in_2[15]), .A(in_1[15]), .Slct(slct), .AorB(out_4[15]));
endmodule

module selectooor (
  input  [35:0] in_1,
  input  [35:0] in_2,
  input  slct,
  output [35:0] out_4
);

  selector selector_1 (.B(in_2[0]), .A(in_1[0]), .Slct(slct), .AorB(out_4[0]));
  selector selector_2 (.B(in_2[1]), .A(in_1[1]), .Slct(slct), .AorB(out_4[1]));
  selector selector_3 (.B(in_2[2]), .A(in_1[2]), .Slct(slct), .AorB(out_4[2]));
  selector selector_4 (.B(in_2[3]), .A(in_1[3]), .Slct(slct), .AorB(out_4[3]));
  selector selector_5 (.B(in_2[4]), .A(in_1[4]), .Slct(slct), .AorB(out_4[4]));
  selector selector_6 (.B(in_2[5]), .A(in_1[5]), .Slct(slct), .AorB(out_4[5]));
  selector selector_7 (.B(in_2[6]), .A(in_1[6]), .Slct(slct), .AorB(out_4[6]));
  selector selector_8 (.B(in_2[7]), .A(in_1[7]), .Slct(slct), .AorB(out_4[7]));
  selector selector_9 (.B(in_2[8]), .A(in_1[8]), .Slct(slct), .AorB(out_4[8]));
  selector selector_10 (.B(in_2[9]), .A(in_1[9]), .Slct(slct), .AorB(out_4[9]));
  selector selector_11 (.B(in_2[10]), .A(in_1[10]), .Slct(slct), .AorB(out_4[10]));
  selector selector_12 (.B(in_2[11]), .A(in_1[11]), .Slct(slct), .AorB(out_4[11]));
  selector selector_13 (.B(in_2[12]), .A(in_1[12]), .Slct(slct), .AorB(out_4[12]));
  selector selector_14 (.B(in_2[13]), .A(in_1[13]), .Slct(slct), .AorB(out_4[13]));
  selector selector_15 (.B(in_2[14]), .A(in_1[14]), .Slct(slct), .AorB(out_4[14]));
  selector selector_16 (.B(in_2[15]), .A(in_1[15]), .Slct(slct), .AorB(out_4[15]));
  selector selector_17 (.B(in_2[16]), .A(in_1[16]), .Slct(slct), .AorB(out_4[16]));
  selector selector_18 (.B(in_2[17]), .A(in_1[17]), .Slct(slct), .AorB(out_4[17]));
  selector selector_19 (.B(in_2[18]), .A(in_1[18]), .Slct(slct), .AorB(out_4[18]));
  selector selector_20 (.B(in_2[19]), .A(in_1[19]), .Slct(slct), .AorB(out_4[19]));
  selector selector_21 (.B(in_2[20]), .A(in_1[20]), .Slct(slct), .AorB(out_4[20]));
  selector selector_22 (.B(in_2[21]), .A(in_1[21]), .Slct(slct), .AorB(out_4[21]));
  selector selector_23 (.B(in_2[22]), .A(in_1[22]), .Slct(slct), .AorB(out_4[22]));
  selector selector_24 (.B(in_2[23]), .A(in_1[23]), .Slct(slct), .AorB(out_4[23]));
  selector selector_25 (.B(in_2[24]), .A(in_1[24]), .Slct(slct), .AorB(out_4[24]));
  selector selector_26 (.B(in_2[25]), .A(in_1[25]), .Slct(slct), .AorB(out_4[25]));
  selector selector_27 (.B(in_2[26]), .A(in_1[26]), .Slct(slct), .AorB(out_4[26]));
  selector selector_28 (.B(in_2[27]), .A(in_1[27]), .Slct(slct), .AorB(out_4[27]));
  selector selector_29 (.B(in_2[28]), .A(in_1[28]), .Slct(slct), .AorB(out_4[28]));
  selector selector_30 (.B(in_2[29]), .A(in_1[29]), .Slct(slct), .AorB(out_4[29]));
  selector selector_31 (.B(in_2[30]), .A(in_1[30]), .Slct(slct), .AorB(out_4[30]));
  selector selector_32 (.B(in_2[31]), .A(in_1[31]), .Slct(slct), .AorB(out_4[31]));
  selector selector_33 (.B(in_2[32]), .A(in_1[32]), .Slct(slct), .AorB(out_4[32]));
  selector selector_34 (.B(in_2[33]), .A(in_1[33]), .Slct(slct), .AorB(out_4[33]));
  selector selector_35 (.B(in_2[34]), .A(in_1[34]), .Slct(slct), .AorB(out_4[34]));
  selector selector_36 (.B(in_2[35]), .A(in_1[35]), .Slct(slct), .AorB(out_4[35]));
endmodule

module ConttrolN (
  input  [3:0] FLGs,
  input  [7:0] OPcode,
  input  [3:0] Steps,
  output [35:0] x
);

  wire and_1_out, and_2_out, and_3_out, and_4_out, and_5_out, and_6_out, and_7_out, and_8_out, and_9_out,
       and_10_out, and_11_out, and_12_out, and_13_out, and_14_out, and_15_out, and_16_out, and_17_out,
       and_19_out, and_20_out, and_21_out, and_22_out, and_23_out, and_24_out, and_25_out, and_26_out,
       and_27_out, and_28_out, and_30_out, and_31_out, and_32_out, and_33_out, and_34_out, and_35_out,
       and_36_out, and_37_out, and_38_out, and_39_out, not_1_out, not_2_out, not_3_out, not_4_out, not_5_out,
       not_6_out, not_7_out, not_8_out, not_9_out, not_10_out, not_11_out, not_12_out, not_13_out,
       not_14_out, not_15_out, not_16_out;

  not not_1 (not_1_out, FLGs[3]);
  not not_2 (not_2_out, FLGs[2]);
  not not_3 (not_3_out, FLGs[1]);
  not not_4 (not_4_out, FLGs[0]);
  not not_5 (not_5_out, OPcode[7]);
  not not_6 (not_6_out, OPcode[6]);
  not not_7 (not_7_out, OPcode[5]);
  not not_8 (not_8_out, OPcode[4]);
  not not_9 (not_9_out, OPcode[3]);
  not not_10 (not_10_out, OPcode[2]);
  not not_11 (not_11_out, OPcode[1]);
  not not_12 (not_12_out, OPcode[0]);
  not not_13 (not_13_out, Steps[3]);
  not not_14 (not_14_out, Steps[2]);
  not not_15 (not_15_out, Steps[1]);
  not not_16 (not_16_out, Steps[0]);
  and and_1 (and_1_out, not_1_out, not_2_out, FLGs[0], not_5_out, not_6_out, not_7_out, not_8_out, not_9_out, not_10_out, not_11_out, not_12_out, not_13_out, not_14_out, Steps[1], Steps[0]);
  and and_2 (and_2_out, not_1_out, not_2_out, FLGs[1], not_5_out, not_6_out, not_7_out, not_8_out, not_9_out, not_10_out, not_11_out, not_12_out, not_13_out, not_14_out, Steps[1], Steps[0]);
  and and_3 (and_3_out, not_1_out, not_2_out, not_3_out, not_4_out, not_5_out, not_6_out, not_7_out, not_8_out, not_9_out, not_10_out, not_11_out, not_12_out, Steps[3], not_14_out, not_15_out, not_16_out);
  and and_4 (and_4_out, not_1_out, not_2_out, FLGs[0], not_5_out, not_6_out, not_7_out, not_8_out, not_9_out, not_10_out, not_11_out, not_12_out, not_13_out, not_14_out, Steps[1], Steps[0]);
  and and_5 (and_5_out, not_1_out, not_2_out, FLGs[1], not_5_out, not_6_out, not_7_out, not_8_out, not_9_out, not_10_out, not_11_out, not_12_out, not_13_out, not_14_out, Steps[1], Steps[0]);
  and and_6 (and_6_out, not_1_out, not_2_out, not_3_out, not_4_out, not_5_out, not_6_out, not_7_out, not_8_out, not_9_out, not_10_out, not_11_out, not_12_out, Steps[3], not_14_out, not_15_out, not_16_out);
  and and_7 (and_7_out, not_1_out, not_2_out, FLGs[0], not_5_out, not_6_out, not_7_out, not_8_out, not_9_out, not_10_out, not_11_out, not_12_out, not_13_out, not_14_out, Steps[1], not_16_out);
  and and_8 (and_8_out, not_1_out, not_2_out, FLGs[1], not_5_out, not_6_out, not_7_out, not_8_out, not_9_out, not_10_out, not_11_out, not_12_out, not_13_out, not_14_out, Steps[1], not_16_out);
  and and_9 (and_9_out, not_1_out, not_2_out, not_3_out, not_4_out, not_5_out, not_6_out, not_7_out, not_8_out, not_9_out, not_10_out, not_11_out, not_12_out, not_13_out, Steps[2], Steps[1], Steps[0]);
  and and_10 (and_10_out, not_1_out, not_2_out, not_5_out, not_6_out, not_7_out, not_8_out, not_9_out, not_10_out, not_11_out, not_13_out, not_14_out, not_15_out, Steps[0]);
  and and_11 (and_11_out, not_1_out, not_2_out, FLGs[0], not_5_out, not_6_out, not_7_out, not_8_out, not_9_out, not_10_out, not_11_out, not_12_out, not_13_out, not_14_out, Steps[1], not_16_out);
  and and_12 (and_12_out, not_1_out, not_2_out, FLGs[1], not_5_out, not_6_out, not_7_out, not_8_out, not_9_out, not_10_out, not_11_out, not_12_out, not_13_out, not_14_out, Steps[1], not_16_out);
  and and_13 (and_13_out, not_1_out, not_2_out, not_3_out, not_4_out, not_5_out, not_6_out, not_7_out, not_8_out, not_9_out, not_10_out, not_11_out, not_13_out, Steps[0]);
  and and_14 (and_14_out, not_1_out, not_2_out, not_5_out, not_6_out, not_7_out, not_8_out, not_9_out, not_10_out, not_11_out, OPcode[0], not_13_out, Steps[0]);
  and and_15 (and_15_out, not_1_out, not_2_out, not_5_out, not_6_out, not_7_out, not_8_out, not_9_out, not_10_out, not_11_out, not_13_out, not_14_out, not_15_out, not_16_out);
  and and_16 (and_16_out, not_1_out, not_2_out, not_3_out, not_4_out, not_5_out, not_6_out, not_7_out, not_8_out, not_9_out, not_10_out, not_11_out, not_13_out, not_16_out);
  and and_17 (and_17_out, not_1_out, not_2_out, not_5_out, not_6_out, not_7_out, not_8_out, not_9_out, not_10_out, not_11_out, OPcode[0], not_13_out, not_16_out);
  and and_18 (x[13], not_1_out, not_2_out, not_5_out, not_6_out, not_7_out, not_8_out, not_9_out, not_10_out, not_11_out, not_13_out, not_14_out, not_15_out, Steps[0]);
  and and_19 (and_19_out, not_1_out, not_2_out, not_5_out, not_6_out, not_7_out, not_8_out, not_9_out, not_10_out, not_11_out, not_13_out, not_14_out, not_15_out, Steps[0]);
  and and_20 (and_20_out, not_1_out, not_2_out, not_3_out, not_4_out, not_5_out, not_6_out, not_7_out, not_8_out, not_9_out, not_10_out, not_11_out, not_13_out, not_14_out, Steps[0]);
  and and_21 (and_21_out, not_1_out, not_2_out, not_3_out, not_4_out, not_5_out, not_6_out, not_7_out, not_8_out, not_9_out, not_10_out, not_11_out, not_13_out, not_15_out, Steps[0]);
  and and_22 (and_22_out, not_1_out, not_2_out, not_5_out, not_6_out, not_7_out, not_8_out, not_9_out, not_10_out, not_11_out, OPcode[0], not_13_out, not_14_out, Steps[0]);
  and and_23 (and_23_out, not_1_out, not_2_out, not_5_out, not_6_out, not_7_out, not_8_out, not_9_out, not_10_out, not_11_out, OPcode[0], not_13_out, not_15_out, Steps[0]);
  and and_24 (and_24_out, not_1_out, not_2_out, not_5_out, not_6_out, not_7_out, not_8_out, not_9_out, not_10_out, not_11_out, not_13_out, not_14_out, not_15_out, not_16_out);
  and and_25 (and_25_out, not_1_out, not_2_out, not_3_out, not_4_out, not_5_out, not_6_out, not_7_out, not_8_out, not_9_out, not_10_out, not_11_out, not_13_out, not_14_out, not_16_out);
  and and_26 (and_26_out, not_1_out, not_2_out, not_3_out, not_4_out, not_5_out, not_6_out, not_7_out, not_8_out, not_9_out, not_10_out, not_11_out, not_13_out, not_15_out, not_16_out);
  and and_27 (and_27_out, not_1_out, not_2_out, not_5_out, not_6_out, not_7_out, not_8_out, not_9_out, not_10_out, not_11_out, OPcode[0], not_13_out, not_14_out, not_16_out);
  and and_28 (and_28_out, not_1_out, not_2_out, not_5_out, not_6_out, not_7_out, not_8_out, not_9_out, not_10_out, not_11_out, OPcode[0], not_13_out, not_15_out, not_16_out);
  and and_29 (x[8], not_1_out, not_2_out, not_5_out, not_6_out, not_7_out, not_8_out, not_9_out, not_10_out, not_11_out, OPcode[0], not_13_out, Steps[2], Steps[1], Steps[0]);
  and and_30 (and_30_out, not_1_out, not_2_out, not_3_out, not_4_out, not_5_out, not_6_out, not_7_out, not_8_out, not_9_out, not_10_out, not_11_out, not_13_out, not_14_out, Steps[1], Steps[0]);
  and and_31 (and_31_out, not_1_out, not_2_out, not_5_out, not_6_out, not_7_out, not_8_out, not_9_out, not_10_out, not_11_out, OPcode[0], not_13_out, not_14_out, Steps[1], Steps[0]);
  and and_32 (and_32_out, not_1_out, not_2_out, not_3_out, not_4_out, not_5_out, not_6_out, not_7_out, not_8_out, not_9_out, not_10_out, not_11_out, not_13_out, Steps[2], not_15_out, Steps[0]);
  and and_33 (and_33_out, not_1_out, not_2_out, not_5_out, not_6_out, not_7_out, not_8_out, not_9_out, not_10_out, not_11_out, OPcode[0], not_13_out, Steps[2], not_15_out, Steps[0]);
  and and_34 (and_34_out, not_1_out, not_2_out, not_3_out, not_4_out, not_5_out, not_6_out, not_7_out, not_8_out, not_9_out, not_10_out, not_11_out, not_13_out, Steps[2], Steps[1], not_16_out);
  and and_35 (and_35_out, not_1_out, not_2_out, not_5_out, not_6_out, not_7_out, not_8_out, not_9_out, not_10_out, not_11_out, OPcode[0], not_13_out, Steps[2], Steps[1], not_16_out);
  and and_36 (and_36_out, not_1_out, not_2_out, FLGs[0], not_5_out, not_6_out, not_7_out, not_8_out, not_9_out, not_10_out, not_11_out, not_12_out, not_13_out, Steps[2], not_15_out, not_16_out);
  and and_37 (and_37_out, not_1_out, not_2_out, FLGs[1], not_5_out, not_6_out, not_7_out, not_8_out, not_9_out, not_10_out, not_11_out, not_12_out, not_13_out, Steps[2], not_15_out, not_16_out);
  and and_38 (and_38_out, not_1_out, not_2_out, not_5_out, not_6_out, not_7_out, not_8_out, not_9_out, not_10_out, not_11_out, OPcode[0], Steps[3], not_14_out, not_15_out, not_16_out);
  and and_39 (and_39_out, not_1_out, not_2_out, not_3_out, not_4_out, not_5_out, not_6_out, not_7_out, not_8_out, not_9_out, not_10_out, not_11_out, not_12_out, Steps[3], not_14_out, not_15_out, Steps[0]);
  or or_1 (x[26], and_1_out, and_2_out, and_3_out);
  or or_2 (x[23], and_4_out, and_5_out, and_6_out);
  or or_3 (x[22], and_7_out, and_8_out, and_9_out);
  or or_4 (x[15], and_10_out, and_11_out, and_12_out, and_13_out, and_14_out);
  or or_5 (x[14], and_15_out, and_16_out, and_17_out);
  or or_6 (x[10], and_19_out, and_20_out, and_21_out, and_22_out, and_23_out);
  or or_7 (x[9], and_24_out, and_25_out, and_26_out, and_27_out, and_28_out);
  or or_8 (x[5], and_30_out, and_31_out);
  or or_9 (x[4], and_32_out, and_33_out);
  or or_10 (x[3], and_34_out, and_35_out);
  or or_11 (x[2], and_36_out, and_37_out, and_38_out, and_39_out);

  assign {x[35:27], x[25:24], x[21:16], x[12:11], x[7:6], x[1:0]} = {23{1'b0}};
endmodule
